# Fritzing sketch SketchClient (saved by Fritzing 0.9.2b)
breadboards: 2

parts:
  Componente1 = Arduino Uno (Rev3)
  S1 = Pushbutton [package="[THT]"]
  LED4 = LED - 3mm [color="Red (633nm)" package="3 mm [THT]"]
  LED5 = LED - 3mm [color="Red (633nm)" package="3 mm [THT]"]
  LED6 = LED - 3mm [color="Red (633nm)" package="3 mm [THT]"]
  LED7 = LED - 3mm [color="Red (633nm)" package="3 mm [THT]"]
  LED8 = LED - 3mm [color="Red (633nm)" package="3 mm [THT]"]
  LED9 = LED - 3mm [color="Red (633nm)" package="3 mm [THT]"]
  U1 = 74HC4067 [package=ssop24]
  LED10 = LED - 3mm [color="Red (633nm)" package="3 mm [THT]"]
  LED11 = LED - 3mm [color="Red (633nm)" package="3 mm [THT]"]
  LED12 = LED - 3mm [color="Red (633nm)" package="3 mm [THT]"]
  LED13 = LED - 3mm [color="Red (633nm)" package="3 mm [THT]"]
  LED14 = LED - 3mm [color="Red (633nm)" package="3 mm [THT]"]
  LED15 = LED - 3mm [color="Red (633nm)" package="3 mm [THT]"]
  LED16 = LED - 3mm [color="Red (633nm)" package="3 mm [THT]"]
  LED17 = RGB LED - (4 legs) [package="5 mm [THT]"]
  R1 = Resistor [tolerance=±5% resistance=220 package=THT]
  R2 = Resistor [tolerance=±5% resistance=220 package=THT]
  R3 = Resistor [tolerance=±5% resistance=220 package=THT]
  R4 = Resistor [tolerance=±5% resistance=220 package=THT]
  Componente2 = SRF05 Ultrasonic Rangefinder
  SG1 = Buzzer 12mm [package=buzzer-12mm-ns]
  R5 = Rotary Potentiometer (Small) [maximum_resistance=100kΩ package=THT]

nets:
  VCC: Componente1.D8, Componente1.D7, U1.VCC, Componente2.VCC, Componente2.Trig, Componente2.Echo
  N1: Componente1.D9_PWM, R3.Pin_0
  N2: Componente1.D10_PWM/SS, R2.Pin_0
  N3: Componente1.D11_PWM/MOSI, R1.Pin_0
  N4: Componente1.D12/MISO, U1.S2
  N5: Componente1.D13/SCK, U1.S3
  N6: Componente1.D2, S1.Pin_1, S1.Pin_2
  N7: Componente1.D3_PWM, R5.wiper
  N8: Componente1.D4, U1.S0
  N9: Componente1.D5_PWM, U1.S1
  N10: Componente1.D6_PWM, R4.Pin_0
  N11: Componente1.GND, S1.Pin_3, S1.Pin_4, LED16.cathode, LED17.common_anode
  N12: LED4.cathode, LED5.cathode, LED6.cathode, U1.GND, LED13.cathode, LED14.cathode, LED15.cathode, SG1.1
  N13: LED4.anode, U1.CHAN0
  N14: LED5.anode, U1.CHAN1
  N15: LED6.anode, U1.CHAN2
  N16: LED7.cathode, LED8.cathode, LED9.cathode, U1.EN, LED10.cathode, LED11.cathode, LED12.cathode, Componente2.GND, R5.leg2
  N17: LED7.anode, U1.CHAN4
  N18: LED8.anode, U1.CHAN5
  N19: LED9.anode, U1.CHAN3
  N20: U1.CHAN7, LED14.anode
  N21: U1.CHAN6, LED13.anode
  N22: U1.CHAN11, LED10.anode
  N23: U1.CHAN10, LED11.anode
  N24: U1.CHAN9, LED12.anode
  N25: U1.CHAN8, LED15.anode
  N26: LED16.anode, R4.Pin_1
  N27: LED17.red_cathode, R3.Pin_1
  N28: LED17.green_cathode, R2.Pin_1
  N29: LED17.blue_cathode, R1.Pin_1
  N30: SG1.2, R5.leg1
